# Fritzing sketch Model (saved by Fritzing 0.9.3b)
breadboards: 1

parts:
  U1 = NodeMCU V3.0
  LED2 = smd LED [color="Red (633nm)" package="1206 [SMD]"]
  R1 = Resistor [tolerance=±5% resistance=220 package="0805 [SMD]"]

nets:
  N1: U1.D0, LED2.anode
  N2: U1.GND, R1.Pin_1
  N3: LED2.cathode, R1.Pin_0

custom parts:
  NodeMCU V3.0: NodeMcu V3 Lua WIFI Development Board
